# Fritzing sketch DesignlabSketch (saved by Fritzing 0.9.2b)

parts:
  Raspberry_Pi = Raspberry Pi 2
  TFT_Screen = Adafruit PiTFT Plus 2.8inch
  ADC = Adafruit ADS1115 16Bit I2C ADC
  U1 = LIPO-2000mAh [package=lipo-2000]
  Slider1 = SLIDER [package=slider]
  Slider2 = SLIDER [package=slider]
  Microphone = USB Connectors [package=usb-a-s-nosilk-female]  # not connected
  Slider3 = SLIDER [package=slider]

nets:
  3V3: Raspberry_Pi.3v3, Raspberry_Pi.3V3, TFT_Screen.3.3V, ADC.VDD, Slider1.E, Slider2.E, Slider3.E
  N1: Raspberry_Pi.GPIO2, ADC.SDA
  N2: Raspberry_Pi.GPIO3, ADC.SCL
  N3: Raspberry_Pi.GPIO10, TFT_Screen.MOSI_
  N4: Raspberry_Pi.GPIO9, TFT_Screen.MISO
  N5: Raspberry_Pi.GPIO11, TFT_Screen.SCLK
  GND: Raspberry_Pi.GND, ADC.GND, U1.-, Slider1.A, Slider2.A, Slider3.A
  N6: Raspberry_Pi.GPIO7, TFT_Screen.RT_CS
  N7: Raspberry_Pi.GPIO8, TFT_Screen.TFT_CS
  N8: Raspberry_Pi.GPIO25, TFT_Screen.TFT_DC
  5V: Raspberry_Pi.5V, TFT_Screen.+5V, U1.+
  N9: ADC.AIN2, Slider3.S
  N10: ADC.AIN1, Slider2.S
  N11: ADC.AIN0, Slider1.S

custom parts:
  Adafruit PiTFT Plus 2.8inch: Is this not the cutest little display for the Raspberry Pi? It features a 2.8" display with 320x240 16-bit color pixels and a resistive touch overlay. The plate uses the high speed SPI interface on the Pi and can use the mini display as a console, X window port, displaying images or video etc. Best of all it plugs right in on top! This updated design fits perfectly onto the Pi Zero, Pi 3, Pi 2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
  Adafruit ADS1115 16Bit I2C ADC: For microcontrollers without an analog-to-digital converter or when you want a higher-precision ADC, the ADS1115 provides 16-bit precision at 860 samples/second over I2C. The chip can be configured as 4 single-ended input channels, or two differential channels. As a nice bonus, it even includes a programmable gain amplifier, up to x16, to help boost up smaller single/differential signals to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
